// Digital circuit TBOS Testing.dig as structural Verilog
module TBOS_Testing (
  input  clk
);

  wire button_1_out, button_2_out, button_3_out, telescope_computing_system_1_os_running;
  wire [15:0] Drive_1_d, Drive_2_d, Keyboard_0_d, Root_Drive_d, TBOS_1_1_d,
       telescope_computing_system_1_os_adr, telescope_computing_system_1_status_code,
       telescope_computing_system_1_tk1_out;
  wire [16:16] Keyboard_0_av;
  wire [18:16] telescope_computing_system_1_tk1_out_2;
  wire [19:0] telescope_computing_system_1_tnet_o_1, telescope_computing_system_1_tnet_o_2;
  wire [33:0] telescope_computing_system_1_d0_out, telescope_computing_system_1_d1_out,
       telescope_computing_system_1_d2_out;

  LED OS_Is_Running (.in(telescope_computing_system_1_os_running));
  // Probe Status on telescope_computing_system_1_status_code
  Telescope_Computing_System telescope_computing_system_1 (
    .OS_Running(telescope_computing_system_1_os_running),
    .Status_Code(telescope_computing_system_1_status_code), .Power_On(button_1_out), .Clock_Input(clk),
    .Pause(button_2_out), .PAUS_Mode(1'b1), .STOP(button_3_out),
    .OS_Adr(telescope_computing_system_1_os_adr), .OS_In(TBOS_1_1_d), .D0_In(Root_Drive_d),
    .D0_Out(telescope_computing_system_1_d0_out), .D1_In(Drive_1_d),
    .D1_Out(telescope_computing_system_1_d1_out), .D2_In(Drive_2_d),
    .D2_Out(telescope_computing_system_1_d2_out), .D3_In({16{1'b0}}), .TNET_I_0({20{1'b0}}),
    .TNET_O_1(telescope_computing_system_1_tnet_o_1), .TNET_I_1(telescope_computing_system_1_tnet_o_1),
    .TNET_O_2(telescope_computing_system_1_tnet_o_2), .TNET_I_2(telescope_computing_system_1_tnet_o_2),
    .TNET_I_3({20{1'b0}}), .K0_In({17{1'b0}}),
    .TK1_Out({telescope_computing_system_1_tk1_out_2, telescope_computing_system_1_tk1_out}),
    .K1_In({Keyboard_0_av[16], Keyboard_0_d}), .K2_In({17{1'b0}}), .K3_In({17{1'b0}}), .GPI_0({18{1'b0}}),
    .GPI_1({18{1'b0}}), .GPI_2({18{1'b0}}), .GPI_3({18{1'b0}}));  // open: D3_Out, TNET_O_0, TNET_O_3, TK0_Out, TK2_Out, TK3_Out, GPO_0, GPO_1, GPO_2, GPO_3
  Button button_1 (.out(button_1_out));
  Button button_2 (.out(button_2_out));
  Button button_3 (.out(button_3_out));
  Keyboard Keyboard_0 (
    .C(telescope_computing_system_1_tk1_out_2[18]), .en(telescope_computing_system_1_tk1_out_2[16]),
    .D(Keyboard_0_d), .av(Keyboard_0_av[16]));
  Terminal terminal_1 (
    .D(telescope_computing_system_1_tk1_out), .C(telescope_computing_system_1_tk1_out_2[18]),
    .en(telescope_computing_system_1_tk1_out_2[17]));
  // Probe OS Boot Drive Address on telescope_computing_system_1_os_adr
  ROM #(.AddrBits(16), .Bits(16)) TBOS_1_1 (.A(telescope_computing_system_1_os_adr), .sel(1'b1), .D(TBOS_1_1_d));
  EEPROMDualPort #(.AddrBits(16), .Bits(16)) Root_Drive (
    .A(telescope_computing_system_1_d0_out[31:16]), .Din(telescope_computing_system_1_d0_out[15:0]),
    .str(telescope_computing_system_1_d0_out[32]), .C(telescope_computing_system_1_d0_out[33]), .ld(1'b1),
    .D(Root_Drive_d));
  EEPROMDualPort #(.AddrBits(16), .Bits(16)) Drive_1 (
    .A(telescope_computing_system_1_d1_out[31:16]), .Din(telescope_computing_system_1_d1_out[15:0]),
    .str(telescope_computing_system_1_d1_out[32]), .C(telescope_computing_system_1_d1_out[33]), .ld(1'b1),
    .D(Drive_1_d));
  EEPROMDualPort #(.AddrBits(16), .Bits(16)) Drive_2 (
    .A(telescope_computing_system_1_d2_out[31:16]), .Din(telescope_computing_system_1_d2_out[15:0]),
    .str(telescope_computing_system_1_d2_out[32]), .C(telescope_computing_system_1_d2_out[33]), .ld(1'b1),
    .D(Drive_2_d));

  // Notes on the sheet:
  //   clk: Hz: 1024
  //   contents of TBOS_1_1 (hex, n*v repeats v):
  //   3f5,4600,e6,226*0,a654,a754,5000,1,50a0,f000,3090,50a0,e000,3090
  //   ,5010,3f5,5000,400,ae10,b912,5000,40,bb01,3078,b974,4600,3cc,50a0
  //   ,0,3078,b974,4600,357,d961,4a00,108,5000,ff00,4600,119,3006,50a0
  //   ,c,3078,b974,4600,293,5000,2,50a0,f000,3090,b000,7000,13,4600
  //   ,120,50a0,e800,3090,50a0,f000,3090,0,b100,6000,12,9200,4000,159
  //   ,b100,6000,13,b901,5010,10,af01,3010,5020,1,ad12,6011,2,d61f,4a00
  //   ,129,7000,13,bd0c,5010,14,a901,60e0,a,50f0,15d,50d0,200,60c0,b
  //   ,60a0,8,60b0,9,6070,7,6060,6,6050,5,6040,4,6030,3,6020,2,6010
  //   ,1,6000,0,1000,5000,600d,4600,119,7000,d8,5000,d8,7010,1,7020
  //   ,2,70a0,8,5000,700,a10a,b508,db04,4000,17b,db05,4000,206,db06
  //   ,4000,1a4,db07,4000,1a4,5000,ff01,4600,119,b100,6000,13,bd0c,5010
  //   ,14,a901,5010,d8,6021,0,7020,0,6021,1,7020,1,6021,2,7020,2,6021
  //   ,8,7020,8,7030,3,7040,4,7050,5,7060,6,7070,7,70b0,9,70e0,a,4600
  //   ,120,b100,6000,13,b010,5070,120,4600,1ac,bbb1,707b,0,3020,bd21
  //   ,6032,2,9210,4000,1cb,5040,f0,8143,4000,1cb,bbb2,702b,0,703b,1
  //   ,b544,3004,3078,b974,4600,1ac,602b,0,603b,1,b9b2,9210,4800,1d2
  //   ,3078,b974,4600,303,5040,f,8143,4000,1e7,bbb2,702b,0,703b,1,3004
  //   ,b010,3078,b974,4600,1ac,602b,0,603b,1,b9b2,b73f,7032,2,be21,bd2c
  //   ,b92b,6002,14,5030,400,3010,ae13,5020,ff,a102,b408,ae03,3078,b974
  //   ,4600,3d3,b100,6000,12,bb01,7000,12,607b,0,b9b1,3087,5020,d8,6012
  //   ,0,6002,1,db12,4000,17b,7032,3,7042,4,7052,5,7062,6,7072,7,70b2
  //   ,9,b1b0,db10,4000,228,db11,4000,228,5010,ff02,7010,6,4600,27c
  //   ,3041,3050,b100,6000,12,5010,10,cb01,4900,264,5000,d8,6010,8,5020
  //   ,e000,a121,b52d,db20,4800,270,d51b,4800,245,303a,b130,9533,4000
  //   ,268,db41,4800,24e,5070,253,3005,30a1,4600,33d,30a1,3078,b974
  //   ,4600,357,d961,4200,26c,db61,4100,274,50a0,c,3006,3078,b974,4600
  //   ,293,5060,a1,4600,276,5060,f001,4600,276,5060,f002,4600,276,5060
  //   ,f000,4600,276,5060,f003,4600,276,5060,f004,5000,d8,7060,6,4600
  //   ,27c,5000,d8,60b0,9,60a0,8,6070,7,6060,6,6050,5,6040,4,6030,3
  //   ,6020,2,6010,1,6000,0,1000,bbb1,70ab,0,b010,b911,3021,bd21,6032
  //   ,2,d63f,4200,297,b130,b63f,7032,2,b120,6022,12,b921,7022,12,3021
  //   ,bd2c,5030,14,a923,b130,7032,0,7032,1,7032,2,7032,3,7032,4,7032
  //   ,5,7032,6,7032,7,7032,a,7032,9,603b,0,7032,8,7002,b,3001,3060
  //   ,b9b1,4600,2ce,9200,4000,302,3010,bd11,6021,2,5030,f0,a033,a123
  //   ,5030,f00,a033,a123,b130,6033,13,3043,b448,a224,7021,2,bd31,6023
  //   ,2,5010,f,8112,4800,2f1,a220,7023,2,3087,bd11,6021,2,5030,f0,8132
  //   ,4000,2fd,b534,3013,4600,2f1,3030,b434,a223,7021,2,3087,9200,4000
  //   ,33c,3010,bd11,6011,2,5020,f00,a121,b528,bd21,6032,2,5040,f,a143
  //   ,cb40,4800,323,5040,f,a044,a134,5040,f0,a141,b544,a234,7032,2
  //   ,3087,5020,f,a123,bd21,6032,2,5040,f0,a143,b544,cb40,4000,333
  //   ,3024,4600,325,5040,f0,a114,b514,a044,a134,a231,7032,2,3087,bbb2
  //   ,707b,0,bd02,b110,b6ad,3091,b7ad,3019,cb01,4900,354,b6ad,3090
  //   ,b7ad,3009,9290,4000,354,700b,1,4600,35d,b160,b9b2,3087,bbb2,707b
  //   ,0,b100,700b,1,b6ad,3090,b7ad,3009,5010,400,ae01,b902,3078,b974
  //   ,4600,396,d961,4200,387,3010,3006,5020,400,ad62,b568,3031,ad32
  //   ,a263,3078,b974,4600,3cc,601b,1,5020,400,ad02,b6ad,3091,b7ad,3019
  //   ,607b,0,b9b2,4600,38c,b060,607b,0,b9b2,3087,9210,4000,395,7090
  //   ,0,b901,9b11,4800,38f,3087,b110,6031,d4,5040,10,3051,af54,c635
  //   ,4200,3b9,5020,1,3051,a952,cb20,4000,3c8,cf54,4800,3af,3065,ae64
  //   ,bf64,6036,d4,3065,af64,c636,4200,3b8,b951,b921,4600,3a4,3015
  //   ,b911,5050,40,cb51,4100,3ca,cf14,4800,39b,3051,ae54,6035,d4,4600
  //   ,39b,3061,3087,b060,3087,b120,6022,e4,7022,3e2,4600,3da,b120,6022
  //   ,e5,7022,3e2,4600,3da,5020,10,3030,ae32,6053,d4,3040,af42,f000
  //   ,b941,9b11,4000,3f2,8f42,4800,3e2,7053,d4,b931,bf34,6053,d4,4600
  //   ,3e2,7053,d4,3087
  //   contents of Root_Drive (hex, n*v repeats v):
  //   16,4600,2,5000,1,5010,1,50a0,800,2000,5010,2,50a0,800,2000,5000
  //   ,2,50a0,9000,2000,4d00,12
  //   Currently running: Multiprogramming Test w/ TSFS Drive 1. 
  //   Root is still loadable.
  //   contents of Drive_1 (hex, n*v repeats v):
  //   8,4,1f,4,3f,4,51,0,16,4600,2,5000,1,5010,1,50a0,800,2000,5010
  //   ,2,50a0,800,2000,5000,2,50a0,9000,2000,4d00,12,0,1f,4600,2,5010
  //   ,24,5000,2,50a0,4800,4500,d,2000,4d00,a,3029,cb21,4000,19,50a0
  //   ,8800,3092,2000,4c00,14,4600,6,50a0,9000,3092,2000,4600,1c,11
  //   ,4600,2,5000,2,50a0,8800,4500,b,2000,4d00,8,3019,50a0,4800,3091
  //   ,4600,4
endmodule
